# Fritzing sketch adc_esp (saved by Fritzing 0.9.3b)
breadboards: 1

parts:
  Componente1 = FTDI Basic Programmer
  Q1 = MOSFET-NCHANNEL [part_number=BS170 package=to-92]
  C1 = Electrolytic Capacitor [capacitance=0.1mF voltage=10V package="100 mil [THT, electrolytic]"]  # not connected
  Componente2 = ADS1015  # not connected
  JP1 = Header 1 [package=1x01_offset]
  R1 = Trimmer Potentiometer [maximum_resistance=10kΩ package=THT]

nets:
  N1: Componente1.DTR, Q1.G
  N2: Componente1.GND, R1.leg1
  N3: Q1.S, JP1.1

notes:
  RTS

custom parts:
  ADS1015: ADC ADS1015
